# Fritzing sketch light_controls (saved by Fritzing 0.9.3b)
breadboards: 1

parts:
  Part1 = Arduino Nano (Rev3.0)
  ULN1 = Darlington Driver [package=dil18]
  ULN2 = Darlington Driver [package=dil18]
  BAT1 = BC9VPC [package=bc9vpc]

nets:
  N1: Part1.GND, ULN1.9, ULN2.9, BAT1.V-
  N2: Part1.D2, ULN1.1
  N3: Part1.D3, ULN1.2
  N4: Part1.D4, ULN1.3
  N5: Part1.D5, ULN1.4
  N6: Part1.D6, ULN1.5
  N7: Part1.D7, ULN1.6
  N8: Part1.D8, ULN1.7
  N9: Part1.D9, ULN1.8
  N10: Part1.D10, ULN2.1
  N11: Part1.D11/MOSI, ULN2.2
  N12: Part1.D12/MISO, ULN2.3
  N13: Part1.A3, ULN2.8
  N14: Part1.A2, ULN2.7
  N15: Part1.A1, ULN2.6
  N16: Part1.A0, ULN2.5
  N17: Part1.D13/SCK, ULN2.4
  N18: ULN1.11, ULN1.12, ULN1.13, ULN1.14, ULN1.15, ULN1.16, ULN1.17, ULN1.18, ULN2.11, ULN2.12, ULN2.13, ULN2.14, ULN2.15, ULN2.16, ULN2.17, ULN2.18, BAT1.V+
